// Digital circuit CacheSetAssoc2Way2WPB.dig as structural Verilog
module CacheSetAssoc2Way2WPB (
  input  [31:0] address,
  output hit,
  output [31:0] data
);

  wire w0valid, w1valid;
  wire [8:0] controller_assoc_1_p10;
  wire [19:0] w0tag, w1tag;
  wire [31:0] w0word0, w0word1, w1word0, w1word1;

  // controller_assoc controller_assoc_1: pin names not known; wires that end beside it: address, w0tag, w0valid, w0word0, w1tag, w1valid, w0word1, w1word0, w1word1, controller_assoc_1_p10, hit, data
  CacheSaMwMemory #(.applicationType("IVERILOG")) u_CacheSaMwMemory (
    .addr(controller_assoc_1_p10), .w0valid(w0valid), .w0tag(w0tag), .w0word0(w0word0), .w0word1(w0word1),
    .w1valid(w1valid), .w1tag(w1tag), .w1word0(w1word0), .w1word1(w1word1));
endmodule

/* Code of CacheSaMwMemory:
module CacheSaMwMemory(
    input [8:0] addr,
    output w0valid,
    output [19:0] w0tag,
    output [31:0] w0word0,
    output [31:0] w0word1,
    output w1valid,
    output [19:0] w1tag,
    output [31:0] w1word0,
    output [31:0] w1word1
);

    reg [169:0] memory [0:511];    
    wire [169:0] data;
    
    assign data = memory[addr];
    
    assign w0valid = data[169];
    assign w1valid = data[168];
    assign w0tag = data[167:148];
    assign w1tag = data[147:128];
    
    assign w0word0 = data[127:96];
    assign w0word1 = data[95:64];
    assign w1word0 = data[63:32];
    assign w1word1 = data[31:0];
    
    initial
    begin
        memory[1] = 170'h3_00000_00001_000000e7_000000e8_000000a7_000000a8;
    end
    
endmodule
*/
