// Digital circuit controller_assoc.dig as structural Verilog
module controller_assoc (
  input  [31:0] address,
  input  [21:0] memory_tag0,
  input  memory_valid0,
  input  [31:0] memory_data00,
  input  [21:0] memory_tag1,
  input  memory_valid1,
  input  [31:0] memory_data01,
  input  [31:0] memory_data10,
  input  [31:0] memory_data11,
  output [7:0] index,
  output hit,
  output [31:0] data
);

  wire comparator_1_eq, comparator_2_eq, sel0, sel1;
  wire [1:0] priorityencoder_1_num;

  PriorityEncoder priorityencoder_1 (.in0(sel0), .in1(sel1), .num(priorityencoder_1_num[0]));  // open: any
  Multiplexer #(.Selector_Bits(2), .Bits(32)) multiplexer_1 (
    .sel(priorityencoder_1_num), .in_0(memory_data00), .in_1(memory_data01), .in_2(memory_data10),
    .in_3(memory_data11), .out(data));
  Comparator #(.Bits(22)) comparator_1 (.a(address[31:10]), .b(memory_tag0), .eq(comparator_1_eq));  // open: gt, lt
  Comparator #(.Bits(22)) comparator_2 (.a(address[31:10]), .b(memory_tag1), .eq(comparator_2_eq));  // open: gt, lt
  and and_1 (sel0, memory_valid0, comparator_1_eq);
  and and_2 (sel1, memory_valid1, comparator_2_eq);
  or or_1 (hit, sel0, sel1);
  // Pins of 1 and 2 bits meet at priorityencoder_1_num

  assign index = address[9:2];
endmodule
